# Fritzing sketch ACSideSchematic (saved by Fritzing 0.9.3b)

parts:
  L1 = Inductor [package="400 mil [THT]"]
  L2 = Inductor [package="400 mil [THT]"]
  R1 = Temperature Sensor (Thermistor) [thermistor_type=NTC package=THT]
  R2 = Temperature Sensor (Thermistor) [thermistor_type=NTC package=THT]
  Part1 = Arduino Uno (Rev3) - ICSP
  U1 = MAX6675 [package=so08]
  U2 = MAX6675 [package=so08]
  U3 = RELAY-SOLIDSTATE [package=relay-s108t02]
  U4 = RELAY-SOLIDSTATE [package=relay-s108t02]

nets:
  N1: L1.pin_0, U3.T2
  GND: L1.pin_1, L2.pin_1
  N2: L2.pin_0, U4.T2
  N3: R1.pin_0, U1.T+
  N4: R1.pin_1, U1.T-
  N5: R2.pin_0, U2.T+
  N6: R2.pin_1, U2.T-
  N7: Part1.D12/MISO, U3.+
  N8: Part1.D13/SCK, U4.+
  N9: Part1.GND, U3.-, U4.-
  120V: U3.T1, U4.T1
