# Fritzing sketch arduinoHookup (saved by Fritzing 0.9.3b)

parts:
  Part1 = Arduino Uno (Rev3)
  S1 = Pushbutton [package="[THT]"]
  R2 = Resistor [tolerance=±5% resistance=10k package=THT]
  LED1 = smd LED [color="Red (633nm)" package="1206 [SMD]"]
  R1 = Resistor [tolerance=±5% resistance=220 package=THT]
  U2 = MAX6675 [part_number="MAX13850 or 6675" package=so08]
  R5 = Temperature Sensor (Thermistor) [thermistor_type=NTC package=THT]
  U3 = MAX6675 [part_number="MAX13850 or 6675" package=so08]
  R7 = Temperature Sensor (Thermistor) [thermistor_type=NTC package=THT]
  U5 = RELAY-SOLIDSTATE [package=relay-s108t02]
  U6 = RELAY-SOLIDSTATE [package=relay-s108t02]
  Q1 = MOSFET-NCHANNEL [part_number="2N7000 or NTE-490/491" package=to-92]
  R8 = Resistor [tolerance=±5% resistance=10k package=THT]
  R9 = Resistor [tolerance=±5% resistance=4.7k package=THT]

nets:
  N1: Part1.D8, U2.MISO, U3.MISO
  N2: Part1.D12/MISO, U6.+
  N3: Part1.D13/SCK, U5.+
  N4: Part1.GND, R2.Pin_0, R1.Pin_1, U5.-, U6.-
  N5: Part1.D2, LED1.anode
  N6: Part1.D3_PWM, S1.Pin_1, S1.Pin_2, R2.Pin_1
  N7: LED1.cathode, R1.Pin_0
  N8: U2.T-, R5.pin_0
  N9: U2.T+, R5.pin_1
  N10: U3.T-, R7.pin_1
  N11: U3.T+, R7.pin_0
  5V signal: Q1.D, R8.Pin_0
  3.3V signal: Q1.S, R9.Pin_1
  3.3V: Q1.G, R9.Pin_0
  5V: R8.Pin_1

notes:
  Zero-crossing optoisolated Solid State Relays (SSRs)
  Thermocouple Amplifier MAX31855 breakout board (1-wire)
  Toaster Oven
  Element A/C
  Circuit to SSR
  Thermocouple Probe ends
  toastyOven, An arduino-controlled Toaster, 1.0
  level-shifting circuit for one-wire
  (MAX31850). SPI needs multiple
